// Logisim project Adder_Substractor_8bit.circ as structural Verilog: 1 circuit, main circuit main
module main (
  input  [7:0] B,
  input  in_2,
  input  [7:0] A,
  output out_4,
  output out_5,
  output out_6,
  output out_7,
  output out_8,
  output out_9,
  output out_10,
  output out_11
);

  wire adder_2_cout, adder_3_cout, adder_4_cout, adder_5_cout, adder_6_cout, adder_7_cout, adder_8_cout,
       xor_1_out, xor_2_out, xor_3_out, xor_4_out, xor_5_out, xor_6_out, xor_7_out, xor_8_out;

  xor xor_1 (xor_1_out, in_2, B[7]);
  xor xor_2 (xor_2_out, in_2, B[6]);
  Adder #(.width(1)) adder_1 (.a(xor_1_out), .b(A[7]), .out(out_4), .cin(adder_2_cout));  // open: cout
  xor xor_3 (xor_3_out, in_2, B[5]);
  Adder #(.width(1)) adder_2 (.a(xor_2_out), .b(A[6]), .out(out_5), .cin(adder_3_cout), .cout(adder_2_cout));
  xor xor_4 (xor_4_out, in_2, B[4]);
  Adder #(.width(1)) adder_3 (.a(xor_3_out), .b(A[5]), .out(out_6), .cin(adder_4_cout), .cout(adder_3_cout));
  xor xor_5 (xor_5_out, B[3], in_2);
  Adder #(.width(1)) adder_4 (.a(xor_4_out), .b(A[4]), .out(out_7), .cin(adder_5_cout), .cout(adder_4_cout));
  Adder #(.width(1)) adder_5 (.a(xor_5_out), .b(A[3]), .out(out_8), .cin(adder_6_cout), .cout(adder_5_cout));
  xor xor_6 (xor_6_out, B[2], in_2);
  Adder #(.width(1)) adder_6 (.a(xor_6_out), .b(A[2]), .out(out_9), .cin(adder_7_cout), .cout(adder_6_cout));
  xor xor_7 (xor_7_out, B[1], in_2);
  Adder #(.width(1)) adder_7 (.a(xor_7_out), .b(A[1]), .out(out_10), .cin(adder_8_cout), .cout(adder_7_cout));
  xor xor_8 (xor_8_out, B[0], in_2);
  Adder #(.width(1)) adder_8 (.a(xor_8_out), .b(A[0]), .out(out_11), .cin(in_2), .cout(adder_8_cout));
endmodule
