// Logisim project part1-16bit.circ as structural Verilog: 1 circuit, main circuit main
module main (
  input  E,
  input  [15:0] I,
  input  [1:0] FunSel
);

  wire clock_1_out, not_2_out;
  wire [15:0] adder_1_out, d_ff_16_q, multiplexer_1_out, multiplexer_2_out, multiplexer_3_out, not_1_out;

  Clock clock_1 (.out(clock_1_out));
  Multiplexer #(.width(16), .enable("false")) multiplexer_1 (
    .in0(16'h1), .in1(not_1_out), .out(multiplexer_1_out), .sel(not_2_out));
  assign not_1_out = ~16'h1;  // NOT_Gate not_1, 16 bits wide
  Multiplexer #(.width(16), .enable("false")) multiplexer_2 (
    .in0(I), .in1({16{1'b0}}), .out(multiplexer_2_out), .sel(FunSel[0]));
  Adder #(.width(16)) adder_1 (.a(d_ff_16_q), .b(multiplexer_1_out), .out(adder_1_out), .cin(not_2_out));  // open: cout
  not not_2 (not_2_out, FunSel[0]);
  D_Flip_Flop d_ff_1 (
    .clk(clock_1_out), .D(multiplexer_3_out[15]), .Q(d_ff_16_q[15]), .en(E));  // open: Qn, preset, reset
  Multiplexer #(.width(16), .enable("false")) multiplexer_3 (
    .in0(adder_1_out), .in1(multiplexer_2_out), .out(multiplexer_3_out), .sel(FunSel[1]));
  D_Flip_Flop d_ff_2 (
    .clk(clock_1_out), .D(multiplexer_3_out[14]), .Q(d_ff_16_q[14]), .en(E));  // open: Qn, preset, reset
  D_Flip_Flop d_ff_3 (
    .clk(clock_1_out), .D(multiplexer_3_out[13]), .Q(d_ff_16_q[13]), .en(E));  // open: Qn, preset, reset
  D_Flip_Flop d_ff_4 (
    .clk(clock_1_out), .D(multiplexer_3_out[12]), .Q(d_ff_16_q[12]), .en(E));  // open: Qn, preset, reset
  D_Flip_Flop d_ff_5 (
    .clk(clock_1_out), .D(multiplexer_3_out[11]), .Q(d_ff_16_q[11]), .en(E));  // open: Qn, preset, reset
  D_Flip_Flop d_ff_6 (
    .clk(clock_1_out), .D(multiplexer_3_out[10]), .Q(d_ff_16_q[10]), .en(E));  // open: Qn, preset, reset
  D_Flip_Flop d_ff_7 (
    .clk(clock_1_out), .D(multiplexer_3_out[9]), .Q(d_ff_16_q[9]), .en(E));  // open: Qn, preset, reset
  D_Flip_Flop d_ff_8 (
    .clk(clock_1_out), .D(multiplexer_3_out[8]), .Q(d_ff_16_q[8]), .en(E));  // open: Qn, preset, reset
  D_Flip_Flop d_ff_9 (.clk(clock_1_out), .D(multiplexer_3_out[7]), .Q(d_ff_16_q[7]));  // open: Qn, preset, en, reset
  D_Flip_Flop d_ff_10 (.clk(clock_1_out), .D(multiplexer_3_out[6]), .Q(d_ff_16_q[6]));  // open: Qn, preset, en, reset
  D_Flip_Flop d_ff_11 (
    .clk(clock_1_out), .D(multiplexer_3_out[5]), .Q(d_ff_16_q[5]), .en(E));  // open: Qn, preset, reset
  D_Flip_Flop d_ff_12 (
    .clk(clock_1_out), .D(multiplexer_3_out[4]), .Q(d_ff_16_q[4]), .en(E));  // open: Qn, preset, reset
  D_Flip_Flop d_ff_13 (
    .clk(clock_1_out), .D(multiplexer_3_out[3]), .Q(d_ff_16_q[3]), .en(E));  // open: Qn, preset, reset
  D_Flip_Flop d_ff_14 (
    .clk(clock_1_out), .D(multiplexer_3_out[2]), .Q(d_ff_16_q[2]), .en(E));  // open: Qn, preset, reset
  D_Flip_Flop d_ff_15 (
    .clk(clock_1_out), .D(multiplexer_3_out[1]), .Q(d_ff_16_q[1]), .en(E));  // open: Qn, preset, reset
  D_Flip_Flop d_ff_16 (
    .clk(clock_1_out), .D(multiplexer_3_out[0]), .Q(d_ff_16_q[0]), .en(E));  // open: Qn, preset, reset
endmodule
