// Logisim project part1-8bit.circ as structural Verilog: 1 circuit, main circuit main
module main (
  input  E,
  input  [7:0] I,
  input  [1:0] FunSel,
  input  E_2,
  input  D
);

  wire and_1_out, and_2_out, clock_1_out, clock_2_out, d_ff_1_q, not_1_out, not_3_out, or_1_out;
  wire [7:0] adder_1_out, d_ff_9_q, multiplexer_1_out, multiplexer_2_out, multiplexer_3_out, not_2_out;

  Clock clock_1 (.out(clock_1_out));
  and and_1 (and_1_out, d_ff_1_q, not_1_out);
  not not_1 (not_1_out, E_2);
  and and_2 (and_2_out, E_2, D);
  Clock clock_2 (.out(clock_2_out));
  Multiplexer #(.width(8), .enable("false")) multiplexer_1 (
    .in0(8'h1), .in1(not_2_out), .out(multiplexer_1_out), .sel(not_3_out));
  assign not_2_out = ~8'h1;  // NOT_Gate not_2, 8 bits wide
  Multiplexer #(.width(8), .enable("false")) multiplexer_2 (
    .in0(I), .in1({8{1'b0}}), .out(multiplexer_2_out), .sel(FunSel[0]));
  or or_1 (or_1_out, and_1_out, and_2_out);
  Adder adder_1 (.a(d_ff_9_q), .b(multiplexer_1_out), .out(adder_1_out), .cin(not_3_out));  // open: cout
  not not_3 (not_3_out, FunSel[0]);
  D_Flip_Flop d_ff_1 (.clk(clock_1_out), .D(or_1_out), .Q(d_ff_1_q), .en(1'b1));  // open: Qn, preset, reset
  D_Flip_Flop d_ff_2 (.clk(clock_2_out), .D(multiplexer_3_out[7]), .Q(d_ff_9_q[7]), .en(E));  // open: Qn, preset, reset
  Multiplexer #(.width(8), .enable("false")) multiplexer_3 (
    .in0(adder_1_out), .in1(multiplexer_2_out), .out(multiplexer_3_out), .sel(FunSel[1]));
  D_Flip_Flop d_ff_3 (.clk(clock_2_out), .D(multiplexer_3_out[6]), .Q(d_ff_9_q[6]), .en(E));  // open: Qn, preset, reset
  D_Flip_Flop d_ff_4 (.clk(clock_2_out), .D(multiplexer_3_out[5]), .Q(d_ff_9_q[5]), .en(E));  // open: Qn, preset, reset
  D_Flip_Flop d_ff_5 (.clk(clock_2_out), .D(multiplexer_3_out[4]), .Q(d_ff_9_q[4]), .en(E));  // open: Qn, preset, reset
  D_Flip_Flop d_ff_6 (.clk(clock_2_out), .D(multiplexer_3_out[3]), .Q(d_ff_9_q[3]), .en(E));  // open: Qn, preset, reset
  D_Flip_Flop d_ff_7 (.clk(clock_2_out), .D(multiplexer_3_out[2]), .Q(d_ff_9_q[2]), .en(E));  // open: Qn, preset, reset
  D_Flip_Flop d_ff_8 (.clk(clock_2_out), .D(multiplexer_3_out[1]), .Q(d_ff_9_q[1]), .en(E));  // open: Qn, preset, reset
  D_Flip_Flop d_ff_9 (.clk(clock_2_out), .D(multiplexer_3_out[0]), .Q(d_ff_9_q[0]), .en(E));  // open: Qn, preset, reset
endmodule
