// Logisim project part3.circ as structural Verilog: 3 circuits, main circuit main
// FunSel
module main (
  input  [7:0] A,
  input  [7:0] B,
  input  [3:0] FunSel,
  output [7:0] out_4,
  output z,
  output c,
  output n,
  output o
);

  wire adder_1_cout, and_2_out, and_3_out, and_4_out, and_5_out, and_6_out, and_7_out, and_8_out, and_9_out,
       clock_1_out, multiplexer_1_out, multiplexer_6_out, multiplexer_7_out, multiplexer_13_out,
       multiplexer_15_out, multiplexer_16_out, multiplexer_17_out, nand_1_out, not_3_out, not_4_out,
       not_5_out, not_6_out, not_7_out, not_8_out, not_9_out, not_10_out, not_11_out, not_12_out, not_13_out,
       or_2_out, or_3_out, or_4_out, or_5_out, xor_1_out, xor_2_out, xor_3_out;
  wire [3:0] nor_1_out;
  wire [7:0] adder_1_out, and_1_out, multiplexer_3_out, multiplexer_12_out, not_1_out, not_2_out, or_1_out,
       xor_4_out;

  assign not_1_out = ~A;  // NOT_Gate not_1, 8 bits wide
  Multiplexer #(.select(2), .enable("false")) multiplexer_1 (
    .in0(1'b0), .in1(1'b0), .in2(A[7]), .in3(c), .out(multiplexer_1_out), .sel(FunSel[2:1]));
  assign not_2_out = ~B;  // NOT_Gate not_2, 8 bits wide
  Multiplexer #(.enable("false")) multiplexer_2 (
    .in0(A[6]), .in1(multiplexer_1_out), .out(multiplexer_12_out[7]), .sel(FunSel[0]));
  xor xor_1 (xor_1_out, A[6], A[7]);
  xor xor_2 (xor_2_out, A[0], A[7]);
  Multiplexer #(.width(8), .enable("false")) multiplexer_3 (
    .in0(B), .in1(not_2_out), .out(multiplexer_3_out), .sel(FunSel[1]));
  Multiplexer #(.enable("false")) multiplexer_4 (.in0(A[5]), .in1(A[7]), .out(multiplexer_12_out[6]), .sel(FunSel[0]));
  Adder adder_1 (.a(A), .b(multiplexer_3_out), .out(adder_1_out), .cin(multiplexer_7_out), .cout(adder_1_cout));
  Multiplexer #(.enable("false")) multiplexer_5 (.in0(A[4]), .in1(A[6]), .out(multiplexer_12_out[5]), .sel(FunSel[0]));
  Multiplexer #(.enable("false")) multiplexer_6 (
    .in0(xor_1_out), .in1(xor_2_out), .out(multiplexer_6_out), .sel(FunSel[0]));
  xor xor_3 (xor_3_out, FunSel[1], B[7]);
  Multiplexer #(.enable("false")) multiplexer_7 (.in0(or_2_out), .in1(c), .out(multiplexer_7_out), .sel(FunSel[0]));
  assign and_1_out = A & B;  // AND_Gate and_1, 8 bits wide
  assign or_1_out = A | B;  // OR_Gate or_1, 8 bits wide
  assign xor_4_out = A ^ B;  // XOR_Gate xor_4, 8 bits wide
  Multiplexer #(.enable("false")) multiplexer_8 (.in0(A[2]), .in1(A[4]), .out(multiplexer_12_out[3]), .sel(FunSel[0]));
  Multiplexer #(.enable("false")) multiplexer_9 (.in0(A[3]), .in1(A[5]), .out(multiplexer_12_out[4]), .sel(FunSel[0]));
  not not_3 (not_3_out, A[7]);
  or or_2 (or_2_out, FunSel[0], FunSel[1]);
  Multiplexer #(.enable("false")) multiplexer_10 (.in0(A[1]), .in1(A[3]), .out(multiplexer_12_out[2]), .sel(FunSel[0]));
  not not_4 (not_4_out, xor_3_out);
  not not_5 (not_5_out, adder_1_out[7]);
  Multiplexer #(.enable("false")) multiplexer_11 (.in0(A[0]), .in1(A[2]), .out(multiplexer_12_out[1]), .sel(FunSel[0]));
  and and_2 (and_2_out, not_3_out, adder_1_out[7], not_4_out);
  and and_3 (and_3_out, xor_3_out, not_5_out, A[7]);
  Multiplexer #(.enable("false")) multiplexer_12 (
    .in0(multiplexer_13_out), .in1(A[1]), .out(multiplexer_12_out[0]), .sel(FunSel[0]));
  or or_3 (or_3_out, and_2_out, and_3_out);
  Multiplexer #(.select(2), .enable("false")) multiplexer_13 (
    .in0(1'b0), .in1(1'b0), .in2(1'b0), .in3(c), .out(multiplexer_13_out), .sel(FunSel[2:1]));
  Multiplexer #(.select(4), .width(8), .enable("false")) multiplexer_14 (
    .in0(A), .in1(B), .in2(not_1_out), .in3(not_2_out), .in4(adder_1_out), .in5(adder_1_out),
    .in6(adder_1_out), .in7(and_1_out), .in8(or_1_out), .in9(xor_4_out), .in10(multiplexer_12_out),
    .in11(multiplexer_12_out), .in12(multiplexer_12_out), .in13(multiplexer_12_out),
    .in14(multiplexer_12_out), .in15(multiplexer_12_out), .out(out_4), .sel(FunSel));
  Multiplexer #(.enable("false")) multiplexer_15 (
    .in0(or_3_out), .in1(multiplexer_6_out), .out(multiplexer_15_out), .sel(FunSel[3]));
  not not_6 (not_6_out, FunSel[1]);
  Multiplexer #(.enable("false")) multiplexer_16 (.in0(A[7]), .in1(A[0]), .out(multiplexer_16_out), .sel(FunSel[0]));
  nor nor_1 (nor_1_out[0], out_4[0], out_4[1], out_4[2], out_4[3], out_4[4], out_4[5], out_4[6], out_4[7]);
  nand nand_1 (nand_1_out, FunSel[0], not_6_out, FunSel[2], FunSel[3]);
  Multiplexer #(.enable("false")) multiplexer_17 (
    .in0(adder_1_cout), .in1(multiplexer_16_out), .out(multiplexer_17_out), .sel(FunSel[3]));
  not not_7 (not_7_out, FunSel[0]);
  not not_8 (not_8_out, FunSel[1]);
  not not_9 (not_9_out, FunSel[3]);
  Multiplexer #(.enable("false")) multiplexer_18 (
    .in0(o), .in1(multiplexer_15_out), .out(nor_1_out[3]), .sel(or_5_out));
  and and_4 (and_4_out, FunSel[3], FunSel[1]);
  not not_10 (not_10_out, FunSel[1]);
  and and_5 (and_5_out, not_10_out, FunSel[2], not_11_out);
  not not_11 (not_11_out, FunSel[3]);
  not not_12 (not_12_out, FunSel[3]);
  and and_6 (and_6_out, not_12_out, FunSel[2], not_13_out);
  not not_13 (not_13_out, FunSel[0]);
  Multiplexer #(.enable("false")) multiplexer_19 (
    .in0(c), .in1(multiplexer_17_out), .out(nor_1_out[1]), .sel(or_4_out));
  and and_7 (and_7_out, not_7_out, FunSel[2]);
  and and_8 (and_8_out, FunSel[1], FunSel[2], FunSel[3]);
  and and_9 (and_9_out, not_8_out, FunSel[2], not_9_out);
  Multiplexer #(.enable("false")) multiplexer_20 (.in0(n), .in1(out_4[7]), .out(nor_1_out[2]), .sel(nand_1_out));
  or or_4 (or_4_out, and_4_out, and_5_out, and_6_out);
  or or_5 (or_5_out, and_7_out, and_8_out, and_9_out);
  Clock clock_1 (.out(clock_1_out));
  Register #(.width(4)) u_C (.D(nor_1_out), .en(1'b1), .Q({o, n, c, z}), .clk(clock_1_out));  // open: clr
endmodule

module Register16 (
  input  in_1,
  input  E,
  input  [15:0] I,
  input  [1:0] FunSel,
  output [15:0] out_5
);

  wire not_2_out;
  wire [15:0] adder_1_out, multiplexer_1_out, multiplexer_2_out, multiplexer_3_out, not_1_out;

  Multiplexer #(.width(16), .enable("false")) multiplexer_1 (
    .in0(16'h1), .in1(not_1_out), .out(multiplexer_1_out), .sel(not_2_out));
  assign not_1_out = ~16'h1;  // NOT_Gate not_1, 16 bits wide
  Multiplexer #(.width(16), .enable("false")) multiplexer_2 (
    .in0(I), .in1({16{1'b0}}), .out(multiplexer_2_out), .sel(FunSel[0]));
  Adder #(.width(16)) adder_1 (.a(out_5), .b(multiplexer_1_out), .out(adder_1_out), .cin(not_2_out));  // open: cout
  not not_2 (not_2_out, FunSel[0]);
  D_Flip_Flop d_ff_1 (.clk(in_1), .D(multiplexer_3_out[15]), .Q(out_5[15]), .en(E));  // open: Qn, preset, reset
  Multiplexer #(.width(16), .enable("false")) multiplexer_3 (
    .in0(adder_1_out), .in1(multiplexer_2_out), .out(multiplexer_3_out), .sel(FunSel[1]));
  D_Flip_Flop d_ff_2 (.clk(in_1), .D(multiplexer_3_out[14]), .Q(out_5[14]), .en(E));  // open: Qn, preset, reset
  D_Flip_Flop d_ff_3 (.clk(in_1), .D(multiplexer_3_out[13]), .Q(out_5[13]), .en(E));  // open: Qn, preset, reset
  D_Flip_Flop d_ff_4 (.clk(in_1), .D(multiplexer_3_out[12]), .Q(out_5[12]), .en(E));  // open: Qn, preset, reset
  D_Flip_Flop d_ff_5 (.clk(in_1), .D(multiplexer_3_out[11]), .Q(out_5[11]), .en(E));  // open: Qn, preset, reset
  D_Flip_Flop d_ff_6 (.clk(in_1), .D(multiplexer_3_out[10]), .Q(out_5[10]), .en(E));  // open: Qn, preset, reset
  D_Flip_Flop d_ff_7 (.clk(in_1), .D(multiplexer_3_out[9]), .Q(out_5[9]), .en(E));  // open: Qn, preset, reset
  D_Flip_Flop d_ff_8 (.clk(in_1), .D(multiplexer_3_out[8]), .Q(out_5[8]), .en(E));  // open: Qn, preset, reset
  D_Flip_Flop d_ff_9 (.clk(in_1), .D(multiplexer_3_out[7]), .Q(out_5[7]));  // open: Qn, preset, en, reset
  D_Flip_Flop d_ff_10 (.clk(in_1), .D(multiplexer_3_out[6]), .Q(out_5[6]));  // open: Qn, preset, en, reset
  D_Flip_Flop d_ff_11 (.clk(in_1), .D(multiplexer_3_out[5]), .Q(out_5[5]), .en(E));  // open: Qn, preset, reset
  D_Flip_Flop d_ff_12 (.clk(in_1), .D(multiplexer_3_out[4]), .Q(out_5[4]), .en(E));  // open: Qn, preset, reset
  D_Flip_Flop d_ff_13 (.clk(in_1), .D(multiplexer_3_out[3]), .Q(out_5[3]), .en(E));  // open: Qn, preset, reset
  D_Flip_Flop d_ff_14 (.clk(in_1), .D(multiplexer_3_out[2]), .Q(out_5[2]), .en(E));  // open: Qn, preset, reset
  D_Flip_Flop d_ff_15 (.clk(in_1), .D(multiplexer_3_out[1]), .Q(out_5[1]), .en(E));  // open: Qn, preset, reset
  D_Flip_Flop d_ff_16 (.clk(in_1), .D(multiplexer_3_out[0]), .Q(out_5[0]), .en(E));  // open: Qn, preset, reset
endmodule

module Shifter (
);

  wire clock_1_out, multiplexer_1_out, multiplexer_2_out, multiplexer_3_out, multiplexer_4_out,
       multiplexer_5_out, multiplexer_6_out, multiplexer_7_out, multiplexer_8_out, multiplexer_9_out,
       multiplexer_10_out, undriven_2, undriven_3, undriven_4, xor_1_out;
  wire [1:0] undriven;
  wire [7:0] d_ff_8_q;

  Multiplexer #(.select(2), .enable("false")) multiplexer_1 (
    .in0(1'b0), .in1(1'b0), .in2(d_ff_8_q[7]), .in3(d_ff_8_q[0]), .out(multiplexer_1_out), .sel(undriven));
  Clock clock_1 (.out(clock_1_out));
  Multiplexer #(.enable("false")) multiplexer_2 (
    .in0(d_ff_8_q[6]), .in1(multiplexer_1_out), .out(multiplexer_2_out), .sel(undriven_2));
  D_Flip_Flop d_ff_1 (.clk(clock_1_out), .D(multiplexer_2_out), .Q(d_ff_8_q[7]), .en(1'b1));  // open: Qn, preset, reset
  Multiplexer #(.enable("false")) multiplexer_3 (
    .in0(d_ff_8_q[5]), .in1(d_ff_8_q[7]), .out(multiplexer_3_out), .sel(undriven_2));
  D_Flip_Flop d_ff_2 (.clk(clock_1_out), .D(multiplexer_3_out), .Q(d_ff_8_q[6]), .en(1'b1));  // open: Qn, preset, reset
  Multiplexer #(.enable("false")) multiplexer_4 (
    .in0(d_ff_8_q[4]), .in1(d_ff_8_q[6]), .out(multiplexer_4_out), .sel(undriven_2));
  D_Flip_Flop d_ff_3 (.clk(clock_1_out), .D(multiplexer_4_out), .Q(d_ff_8_q[5]), .en(1'b1));  // open: Qn, preset, reset
  Multiplexer #(.enable("false")) multiplexer_5 (
    .in0(d_ff_8_q[3]), .in1(d_ff_8_q[5]), .out(multiplexer_5_out), .sel(undriven_2));
  D_Flip_Flop d_ff_4 (.clk(clock_1_out), .D(multiplexer_5_out), .Q(d_ff_8_q[4]), .en(1'b1));  // open: Qn, preset, reset
  Multiplexer #(.enable("false")) multiplexer_6 (
    .in0(d_ff_8_q[2]), .in1(d_ff_8_q[4]), .out(multiplexer_6_out), .sel(undriven_2));
  D_Flip_Flop d_ff_5 (.clk(clock_1_out), .D(multiplexer_6_out), .Q(d_ff_8_q[3]), .en(1'b1));  // open: Qn, preset, reset
  Multiplexer #(.enable("false")) multiplexer_7 (
    .in0(d_ff_8_q[1]), .in1(d_ff_8_q[3]), .out(multiplexer_7_out), .sel(undriven_2));
  D_Flip_Flop d_ff_6 (.clk(clock_1_out), .D(multiplexer_7_out), .Q(d_ff_8_q[2]), .en(1'b1));  // open: Qn, preset, reset
  Multiplexer #(.enable("false")) multiplexer_8 (
    .in0(d_ff_8_q[0]), .in1(d_ff_8_q[2]), .out(multiplexer_8_out), .sel(undriven_2));
  xor xor_1 (xor_1_out, undriven_4, undriven_3);
  D_Flip_Flop d_ff_7 (.clk(clock_1_out), .D(multiplexer_8_out), .Q(d_ff_8_q[1]), .en(1'b1));  // open: Qn, preset, reset
  Multiplexer #(.enable("false")) multiplexer_9 (
    .in0(d_ff_8_q[7]), .in1(1'b0), .out(multiplexer_9_out), .sel(xor_1_out));
  Multiplexer #(.enable("false")) multiplexer_10 (
    .in0(multiplexer_9_out), .in1(d_ff_8_q[1]), .out(multiplexer_10_out), .sel(undriven_2));
  D_Flip_Flop d_ff_8 (
    .clk(clock_1_out), .D(multiplexer_10_out), .Q(d_ff_8_q[0]), .en(1'b1));  // open: Qn, preset, reset
endmodule
